# Fritzing sketch termometer digital (saved by Fritzing 0.9.3b)
breadboards: 1

parts:
  Part2 = Intel Galileo
  U2 = LCD-16X2 [package=lcd-16x2]
  T1 = LM35 Temperature Sensor [package="TO92 [THT]"]
  U3 = POT [package=pot_mammoth]

nets:
  N1: Part2.A0, T1.Vout
  N2: Part2.D11_PWM/MOSI, U2.E
  N3: Part2.D12/MISO, U2.RS
  GND: Part2.GND, U2.VSS, U2.R_W, T1.GND
  N4: Part2.D2, U2.DB7
  N5: Part2.D3_PWM, U2.DB6
  N6: Part2.D4, U2.DB5
  N7: Part2.D5_PWM, U2.DB4
  5V: Part2.5V, U2.VDD, T1.+Vs
  N8: U2.VO, U3.A
